// Logisim project PROYECTO ADC.circ as structural Verilog: 1 circuit, main circuit main
module main (
  input  [2:0] in_1,
  input  [3:0] A,
  input  [3:0] B,
  output [3:0] out_4
);

  wire undriven_3;
  wire [3:0] adder_1_out, and_1_out, multiplexer_1_out, not_1_out, or_1_out, subtractor_1_out, undriven,
       undriven_2, xor_1_out;

  BitSelector #(.width(3), .group(4)) bitselector_1 (.in(in_1), .sel(undriven_3));  // open: out
  Adder #(.width(4)) adder_1 (.b(A), .out(adder_1_out));  // open: a, cin, cout
  Subtractor #(.width(4)) subtractor_1 (.a(undriven), .out(subtractor_1_out));  // open: b, bin, bout
  assign and_1_out = A & B;  // AND_Gate and_1, 4 bits wide
  assign or_1_out = undriven | undriven_2;  // OR_Gate or_1, 4 bits wide
  assign not_1_out = ~undriven_2;  // NOT_Gate not_1, 4 bits wide
  assign xor_1_out = B ^ A;  // XOR_Gate xor_1, 4 bits wide
  Multiplexer #(.select(3), .width(4)) multiplexer_1 (
    .in0(and_1_out), .in1(or_1_out), .in2(xor_1_out), .in3(not_1_out), .in4(subtractor_1_out),
    .in5(adder_1_out), .out(multiplexer_1_out), .en(undriven_3));  // open: in6, in7, sel
endmodule
